// Logisim project alu.circ as structural Verilog: 3 circuits, main circuit main
module main (
  input  [31:0] A,
  input  [31:0] B,
  input  [3:0] ALUControl,
  output [3:0] ALUFlags,
  output [31:0] Result
);

  Difference difference_1 (.in_1(A), .in_2(B), .in_3(ALUControl), .Result(Result), .CarryOut(ALUFlags[1]));

  // Other names for the same wires on the sheet: oVerflow = ALUFlags[0]; Carry = ALUFlags[1]; Zero = ALUFlags[2];
  //   Negative = ALUFlags[3]; Ctrl[3:0] = ALUControl

  // Notes on the sheet:
  //   INPUTS to your circuit
  //   DON'T CHANGE THE LOCATIONS OF THE INPUTS AND OUTPUTS!
  //   OUTPUTS from your circuit
endmodule

module Sum (
  input  [31:0] in_1,
  input  [31:0] in_2,
  input  [3:0] in_3,
  output [31:0] Result,
  output CarryOut
);

  wire comparator_1_eq;

  Comparator #(.width(4)) comparator_1 (.a(4'b0111), .b(in_3), .eq(comparator_1_eq));  // open: gt, lt
  Adder #(.width(32)) adder_1 (.a(in_1), .b(in_2), .out(Result), .cout(CarryOut));  // open: cin

  // Notes on the sheet:
  //   In1
  //   In2
  //   Add Control #
  //   ALU Control
endmodule

module Difference (
  input  [31:0] in_1,
  input  [31:0] in_2,
  input  [3:0] in_3,
  output [31:0] Result,
  output CarryOut
);

  wire comparator_1_eq, not_1_out;
  wire [31:0] bitselector_1_out, bitselector_2_out;

  Comparator #(.width(4)) comparator_1 (.a(4'b1000), .b(in_3), .eq(comparator_1_eq));  // open: gt, lt
  BitSelector #(.width(32), .group(32)) bitselector_1 (.in(in_1), .out(bitselector_1_out), .sel(not_1_out));
  BitSelector #(.width(32), .group(32)) bitselector_2 (.in(in_2), .out(bitselector_2_out), .sel(not_1_out));
  not not_1 (not_1_out, comparator_1_eq);
  Subtractor #(.width(32)) subtractor_1 (
    .a(bitselector_1_out), .b(bitselector_2_out), .out(Result), .bout(CarryOut));  // open: bin

  // Notes on the sheet:
  //   In1
  //   In2
  //   Add Control #
  //   ALU Control
  //   If the Control Number is not correct, the result will be 0
endmodule
